// Logisim project Q2Circuit.circ as structural Verilog: 11 circuits, main circuit System
module System (
);

  wire and_2_out, and_3_out, and_4_out, and_5_out, and_6_out, and_7_out, and_8_out, and_9_out, and_10_out,
       and_11_out, and_12_out, and_13_out, button_1_out, button_2_out, button_3_out, clock_1_out,
       clock_3_out, clock_4_out, clock_5_out, clock_6_out, clock_7_out, clock_8_out, comparator_1_eq,
       comparator_2_eq, comparator_3_eq, comparator_4_eq, comparator_5_eq, comparator_6_eq, comparator_7_eq,
       comparator_8_eq, comparator_9_eq, cpu_1_unsupported_instruction, MemRead, MemWrite, or_1_out,
       or_2_out, rgb_video_1_p2, rgb_video_1_p3, RST, s_r_ff_1_q, s_r_ff_1_qn;
  wire [3:0] cpu_1_pc_out_2, cpu_1_pc_out_3;
  wire [4:0] slider_1_out;
  wire [31:0] Address, bit_extender_1_out, bit_extender_2_out, cpu_1_pc_out, Data_in, Data_out, ram_1_dout,
       ram_2_dout, register_1_q, rom_1_data, videoram_for_monochrome_display_1_l_0,
       videoram_for_monochrome_display_1_l_1, videoram_for_monochrome_display_1_l_2,
       videoram_for_monochrome_display_1_l_3, videoram_for_monochrome_display_1_l_4,
       videoram_for_monochrome_display_1_l_5, videoram_for_monochrome_display_1_l_6,
       videoram_for_monochrome_display_1_l_7, videoram_for_monochrome_display_1_l_8,
       videoram_for_monochrome_display_1_l_9, videoram_for_monochrome_display_1_l_10,
       videoram_for_monochrome_display_1_l_11, videoram_for_monochrome_display_1_l_12,
       videoram_for_monochrome_display_1_l_13, videoram_for_monochrome_display_1_l_14,
       videoram_for_monochrome_display_1_l_15, videoram_for_monochrome_display_1_l_16,
       videoram_for_monochrome_display_1_l_17, videoram_for_monochrome_display_1_l_18,
       videoram_for_monochrome_display_1_l_19, videoram_for_monochrome_display_1_l_20,
       videoram_for_monochrome_display_1_l_21, videoram_for_monochrome_display_1_l_22,
       videoram_for_monochrome_display_1_l_23, videoram_for_monochrome_display_1_l_24,
       videoram_for_monochrome_display_1_l_25, videoram_for_monochrome_display_1_l_26,
       videoram_for_monochrome_display_1_l_27, videoram_for_monochrome_display_1_l_28,
       videoram_for_monochrome_display_1_l_29, videoram_for_monochrome_display_1_l_30,
       videoram_for_monochrome_display_1_l_31;

  Clock clock_1 (.out(clock_1_out));
  Hex_Digit_Display hex_digit_display_1 (.value(cpu_1_pc_out[31:28]));  // open: dp
  D_Flip_Flop d_ff_1 (.clk(clock_1_out), .D(1'b1), .Qn(RST));  // open: Q, preset, reset
  Hex_Digit_Display hex_digit_display_2 (.value(cpu_1_pc_out_3));  // open: dp
  Hex_Digit_Display hex_digit_display_3 (.value(cpu_1_pc_out[27:24]));  // open: dp
  // RGB_Video #(.cursor("No Cursor"), .height(32), .scale(8), .width(32)) rgb_video_1: pin names not known; wires that end beside it: RST, rgb_video_1_p2, rgb_video_1_p3, Address[11:7], Address[6:2], Data_out[23:0]
  Clock clock_2 (.out(rgb_video_1_p2));
  and and_1 (rgb_video_1_p3, MemWrite, comparator_1_eq);
  Comparator #(.width(20)) comparator_1 (.a(20'hffff4), .b(Address[31:12]), .eq(comparator_1_eq));  // open: gt, lt
  or or_1 (or_1_out, MemRead, MemWrite);
  Clock clock_3 (.out(clock_3_out));
  Button button_1 (.out(button_1_out));
  Hex_Digit_Display hex_digit_display_4 (.value(cpu_1_pc_out_2));  // open: dp
  Hex_Digit_Display hex_digit_display_5 (.value(cpu_1_pc_out[15:12]));  // open: dp
  and and_2 (and_2_out, comparator_1_eq, or_1_out);
  CPU cpu_1 (
    .hold_in(s_r_ff_1_q), .Reset_in(RST), .Start_Addr_in(32'h400000), .Data_in(Data_in), .Address(Address),
    .Data_out(Data_out), .unsupported_instruction(cpu_1_unsupported_instruction), .MemRead(MemRead),
    .MemWrite(MemWrite), .PC_out({cpu_1_pc_out[31:24], cpu_1_pc_out_3, cpu_1_pc_out_2, cpu_1_pc_out[15:0]}));
  S_R_Flip_Flop s_r_ff_1 (
    .S(cpu_1_unsupported_instruction), .clk(clock_3_out), .R(1'b0), .Q(s_r_ff_1_q), .Qn(s_r_ff_1_qn),
    .reset(button_1_out));  // open: preset
  LED led_1 (.in(s_r_ff_1_q));
  Clock clock_4 (.out(clock_4_out));
  Hex_Digit_Display hex_digit_display_6 (.value(cpu_1_pc_out[11:8]));  // open: dp
  Hex_Digit_Display hex_digit_display_7 (.value(cpu_1_pc_out[7:4]));  // open: dp
  RAM #(.addrWidth(10), .asyncread("true"), .dataWidth(32)) ram_1 (
    .addr(Address[11:2]), .we(rgb_video_1_p3), .oe(1'b1), .clk(clock_5_out), .din(Data_out), .dout(ram_1_dout));
  Clock clock_5 (.out(clock_5_out));
  Counter #(.max('hffffffff), .width(32)) counter_1 (
    .count(s_r_ff_1_qn), .clk(clock_4_out));  // open: load, D, Q, carry, up, clr
  Hex_Digit_Display hex_digit_display_8 (.value(cpu_1_pc_out[3:0]));  // open: dp
  Comparator #(.width(32)) comparator_2 (.a(Address), .b(32'hffff0010), .eq(comparator_2_eq));  // open: gt, lt
  Comparator #(.width(24)) comparator_3 (.a(Address[31:8]), .b(24'hffff80), .eq(comparator_3_eq));  // open: gt, lt
  Comparator #(.width(16)) comparator_4 (.a(Address[31:16]), .b(16'h40), .eq(comparator_4_eq));  // open: gt, lt
  Comparator #(.width(16)) comparator_5 (.a(Address[31:16]), .b(16'h1001), .eq(comparator_5_eq));  // open: gt, lt
  and and_3 (and_3_out, comparator_3_eq, MemWrite);
  and and_4 (and_4_out, comparator_3_eq, MemRead);
  ROM #(.addrWidth(14), .dataWidth(32)) rom_1 (.addr(Address[15:2]), .data(rom_1_data));
  and and_5 (and_5_out, comparator_4_eq, MemRead);
  RAM #(.addrWidth(14), .asyncread("true"), .dataWidth(32)) ram_2 (
    .addr(Address[15:2]), .we(and_6_out), .oe(1'b1), .clk(clock_6_out), .din(Data_out), .dout(ram_2_dout));
  and and_6 (and_6_out, comparator_5_eq, MemWrite);
  Clock clock_6 (.out(clock_6_out));
  or or_2 (or_2_out, MemWrite, MemRead);
  and and_7 (and_7_out, comparator_2_eq, MemWrite);
  and and_8 (and_8_out, comparator_2_eq, MemRead);
  _7_Segment_Display u_7_segment_display_1 (
    .g(register_1_q[14]), .f(register_1_q[13]), .a(register_1_q[8]), .b(register_1_q[9]),
    .e(register_1_q[12]), .d(register_1_q[11]), .c(register_1_q[10]), .dp(register_1_q[15]));
  DotMatrix #(.dotshape("clusterSegment"), .inputtype("row"), .matrixcols(32), .matrixrows(32)) dotmatrix_1 (
    .row0(videoram_for_monochrome_display_1_l_0), .row1(videoram_for_monochrome_display_1_l_1),
    .row2(videoram_for_monochrome_display_1_l_2), .row3(videoram_for_monochrome_display_1_l_3),
    .row4(videoram_for_monochrome_display_1_l_4), .row5(videoram_for_monochrome_display_1_l_5),
    .row6(videoram_for_monochrome_display_1_l_6), .row7(videoram_for_monochrome_display_1_l_7),
    .row8(videoram_for_monochrome_display_1_l_8), .row9(videoram_for_monochrome_display_1_l_9),
    .row10(videoram_for_monochrome_display_1_l_10), .row11(videoram_for_monochrome_display_1_l_11),
    .row12(videoram_for_monochrome_display_1_l_12), .row13(videoram_for_monochrome_display_1_l_13),
    .row14(videoram_for_monochrome_display_1_l_14), .row15(videoram_for_monochrome_display_1_l_15),
    .row16(videoram_for_monochrome_display_1_l_16), .row17(videoram_for_monochrome_display_1_l_17),
    .row18(videoram_for_monochrome_display_1_l_18), .row19(videoram_for_monochrome_display_1_l_19),
    .row20(videoram_for_monochrome_display_1_l_20), .row21(videoram_for_monochrome_display_1_l_21),
    .row22(videoram_for_monochrome_display_1_l_22), .row23(videoram_for_monochrome_display_1_l_23),
    .row24(videoram_for_monochrome_display_1_l_24), .row25(videoram_for_monochrome_display_1_l_25),
    .row26(videoram_for_monochrome_display_1_l_26), .row27(videoram_for_monochrome_display_1_l_27),
    .row28(videoram_for_monochrome_display_1_l_28), .row29(videoram_for_monochrome_display_1_l_29),
    .row30(videoram_for_monochrome_display_1_l_30), .row31(videoram_for_monochrome_display_1_l_31));
  Videoram_for_monochrome_display videoram_for_monochrome_display_1 (
    .Data_In(Data_out), .ld(and_4_out), .Address(Address[6:2]), .str(and_3_out),
    .L_11(videoram_for_monochrome_display_1_l_11), .L_12(videoram_for_monochrome_display_1_l_12),
    .L_13(videoram_for_monochrome_display_1_l_13), .L_14(videoram_for_monochrome_display_1_l_14),
    .L_15(videoram_for_monochrome_display_1_l_15), .L_8(videoram_for_monochrome_display_1_l_8),
    .L_9(videoram_for_monochrome_display_1_l_9), .L_10(videoram_for_monochrome_display_1_l_10),
    .L_19(videoram_for_monochrome_display_1_l_19), .L_20(videoram_for_monochrome_display_1_l_20),
    .L_21(videoram_for_monochrome_display_1_l_21), .L_22(videoram_for_monochrome_display_1_l_22),
    .L_23(videoram_for_monochrome_display_1_l_23), .L_16(videoram_for_monochrome_display_1_l_16),
    .L_17(videoram_for_monochrome_display_1_l_17), .L_18(videoram_for_monochrome_display_1_l_18),
    .L_27(videoram_for_monochrome_display_1_l_27), .L_28(videoram_for_monochrome_display_1_l_28),
    .L_29(videoram_for_monochrome_display_1_l_29), .L_30(videoram_for_monochrome_display_1_l_30),
    .L_31(videoram_for_monochrome_display_1_l_31), .L_24(videoram_for_monochrome_display_1_l_24),
    .L_25(videoram_for_monochrome_display_1_l_25), .L_26(videoram_for_monochrome_display_1_l_26),
    .Data_Out(Data_in), .L_3(videoram_for_monochrome_display_1_l_3),
    .L_4(videoram_for_monochrome_display_1_l_4), .L_5(videoram_for_monochrome_display_1_l_5),
    .L_6(videoram_for_monochrome_display_1_l_6), .L_7(videoram_for_monochrome_display_1_l_7),
    .L_0(videoram_for_monochrome_display_1_l_0), .L_1(videoram_for_monochrome_display_1_l_1),
    .L_2(videoram_for_monochrome_display_1_l_2));
  assign Data_in = and_2_out ? ram_1_dout : 32'bz;  // Controlled_Buffer controlled_buffer_1
  and and_9 (and_9_out, comparator_5_eq, or_2_out);
  Register #(.width(32)) register_1 (.D(Data_out), .en(and_7_out), .Q(register_1_q), .clk(clock_7_out));  // open: clr
  Clock clock_7 (.out(clock_7_out));
  _7_Segment_Display u_7_segment_display_2 (
    .g(register_1_q[6]), .f(register_1_q[5]), .a(register_1_q[0]), .b(register_1_q[1]), .e(register_1_q[4]),
    .d(register_1_q[3]), .c(register_1_q[2]), .dp(register_1_q[7]));
  Button button_2 (.out(button_2_out));
  assign Data_in = and_5_out ? rom_1_data : 32'bz;  // Controlled_Buffer controlled_buffer_2
  assign Data_in = and_9_out ? ram_2_dout : 32'bz;  // Controlled_Buffer controlled_buffer_3
  assign Data_in = and_8_out ? register_1_q : 32'bz;  // Controlled_Buffer controlled_buffer_4
  Slider #(.Direction("right_to_left"), .width(5)) slider_1 (.out(slider_1_out));
  Clock clock_8 (.out(clock_8_out));
  Comparator #(.width(32)) comparator_6 (.a(Address), .b(32'hffff000c), .eq(comparator_6_eq));  // open: gt, lt
  TTY tty_1 (.data(Data_out[6:0]), .clk(clock_8_out), .we(and_10_out), .clr(button_3_out));
  and and_10 (and_10_out, comparator_6_eq, MemWrite);
  Button button_3 (.out(button_3_out));
  Comparator #(.width(32)) comparator_7 (.a(Address), .b(32'hffff0004), .eq(comparator_7_eq));  // open: gt, lt
  and and_11 (and_11_out, comparator_7_eq, MemRead);
  assign bit_extender_1_out = {{27{1'b0}}, slider_1_out};  // Bit_Extender bit_extender_1
  assign Data_in = and_11_out ? bit_extender_1_out : 32'bz;  // Controlled_Buffer controlled_buffer_5
  assign bit_extender_2_out = {{31{button_2_out}}, button_2_out};  // Bit_Extender bit_extender_2
  assign Data_in = and_12_out ? bit_extender_2_out : 32'bz;  // Controlled_Buffer controlled_buffer_6
  and and_12 (and_12_out, comparator_8_eq, MemRead);
  Comparator #(.width(32)) comparator_8 (.a(Address), .b(32'hffff0000), .eq(comparator_8_eq));  // open: gt, lt
  assign Data_in = and_13_out ? 32'h1 : 32'bz;  // Controlled_Buffer controlled_buffer_7
  and and_13 (and_13_out, comparator_9_eq, MemRead);
  Comparator #(.width(32)) comparator_9 (.a(Address), .b(32'hffff0008), .eq(comparator_9_eq));  // open: gt, lt

  // Notes on the sheet:
  //   Reset circuit
  //   Start addr
  //   Data in -->
  //   press to continue
  //   PC
  //   Bitmap Display (Colour)
  //   Address -->
  //   Data out  -->
  //   CPU halted
  //   Clock cycles
  //   contents of rom_1 (hex, n*v repeats v):
  //   fc20117 ffc10113 513 593 613 8000ef 6f fa010113 4112e23 4812c23 517 58c50513 170000ef 517 59450513
  //   164000ef ff00413 1f8000ef fe851ee3 517 59050513 14c000ef f00793 4f12623 4f12423 100793 4f12223
  //   4f12023 2012e23 ffff8537 530000ef 2012a23 797 5bc78793 7ae03 47a303 87a883 c7a803 107a503 147a583
  //   187a603 1c7a683 207a703 247a783 1c12623 612823 1112a23 1012c23 a12e23 2b12023 2c12223 2d12423
  //   2e12623 2f12823 174000ef 2a12c23 3810613 3c10593 ffff8537 42c000ef 3410813 3c10793 4010713 4410693
  //   4810613 4c10593 ffff8537 258000ef ffff0637 1060693 1160613 c10593 3410513 450000ef 4812703 1f00793
  //   fae7d4e3 517 4dc50513 64000ef 517 4e450513 58000ef 3412503 70000ef 517 4dc50513 44000ef 100513
  //   5c12083 5812403 6010113 8067 41f55793 a7c533 40f50533 8067 ffff07b7 a78623 8067 ffff07b7 a00713
  //   e78623 8067 54783 78c63 ffff0737 f70623 150513 54783 fe079ae3 8067 ff010113 41f55813 2d87813 410713
  //   900613 a00593 fff60613 2b567b3 41f7d693 f6c7b3 40d787b3 3078793 f70423 2b54533 fff70713 fc051ee3
  //   80663 ffff07b7 1078623 900793 2c7c263 410793 c787b3 e10693 ffff0637 7c703 e60623 178793 fed79ae3
  //   1010113 8067 ffff07b7 7c503 ff57513 8067 ffff07b7 47c503 ff57513 8067 50693 100793 4b7d463 fff58613
  //   513 ffff0737 a00593 74783 17f793 fe078ce3 474783 ff7f793 f68023 b78a63 168693 150513 fcc51ee3 60513
  //   68023 8067 fff00513 8067 100593 513 ffff0737 900613 100813 2d00893 fff00313 200006f fd078693 4d66063
  //   251693 a686b3 169693 fd078793 d78533 74783 17f793 fe078ce3 474783 ff7f793 fc0518e3 fd0596e3 fd1794e3
  //   30593 fddff06f 2a58533 8067 ffff82b7 2000313 52383 72a023 428293 450513 fff30313 fe0316e3 8067 62783
  //   279793 f50533 52503 5a783 40f55533 157513 8067 fe010113 112e23 812c23 912a23 1212823 1312623 1412423
  //   50913 58493 60413 70993 80a13 62583 259593 b505b3 5a703 4a503 100613 a61633 fff64613 e67633 c5a023
  //   4a703 6a603 c70733 e4a023 42703 9a603 c70733 e42023 4a703 fff70713 1d00613 e67863 6a703 40e00733
  //   e6a023 42703 6e05a63 42603 1f00713 6e60c63 40613 48593 90513 f2dff0ef 50863 42703 800793 af70263
  //   42503 251513 a90933 92703 4a683 100793 d797b3 e7e7b3 f92023 1c12083 1812403 1412483 1012903 c12983
  //   812a03 2010113 8067 9a703 40e00733 e9a023 f85ff06f 7a783 478613 4a703 f70863 178793 fef65ce3
  //   f75ff06f 9a783 40f007b3 f9a023 4a783 6a703 40e787b3 f4a023 42783 9a703 e787b3 f42023 f45ff06f
  //   2092683 4a783 178713 100793 e797b3 fff7c793 d7f7b3 2f92023 9a783 40f007b3 f9a023 179793 42703 f707b3
  //   f42023 a2783 178793 fa2023 f19ff06f 6052e23 62783 1b00713 2f75e63 1b00793 f5a023 713 100813 500613
  //   7c52683 5a783 f707b3 f817b3 d7e7b3 6f52e23 170713 fec712e3 8067 7c663 f5a023 fc9ff06f 5a023 fc1ff06f
  //   52783 a00513 2a7c733 271713 e58733 72703 e62023 2a7e7b3 279793 f585b3 5a783 f6a023 8067 fff00293
  //   2552023 8067 202a2a2a 41455242 54554f4b 2a2a2021 a2a 73657250 54532073 20545241 74747562 a6e6f
  //   20657355 20656874 64696c73 74207265 6f6d206f 74206576 70206568 6c646461 656c2065 6f207466 69722072
  //   21746867 a 202a2a2a 454d4147 45564f20 2a2a2052 a2a 20756f59 6e726165 206465 696f7020 2173746e a 3f 6
  //   5b 4f 66 6d 7d 7 7f 4f 30*0 f8000000
  //   ROM
  //   RAM
  //   Monochrome Bitmap Display
  //   START
  //   PADDLE CONTROL
  //   TDR
  //   RDR
  //   clear
  //   RISC-V RV32IM Computer System model by Pavel Gladyshev
  //   MMIO DIsplay
  //   MMIO Keyboard
  //   licensed under Creative Commons Attribution International license 4.0 
  //   RCR
  //   TCR
  //   Display is always ready
  //   clear
  //   clear
endmodule

// RISC-V RV32IM
module CPU (
  input  [31:0] Start_Addr_in,
  input  Reset_in,
  input  [31:0] Data_in,
  input  hold_in,
  output [31:0] Address,
  output [31:0] Data_out,
  output MemRead,
  output MemWrite,
  output unsupported_instruction,
  output [31:0] PC_out
);

  wire A_B, A_B_signed, A_B_unsigned, clock_1_out, div_by_zero, execute, fetch, in_cache, nor_1_out,
       not_1_out, or_1_out, pipelined_fetch, sel_address_source, sel_byte_out, sel_halfword_out,
       sel_IR_store, sel_reg_write_enable;
  wire [1:0] sel_B_source, sel_PC_increment, sel_PC_source;
  wire [2:0] funct3, sel_muldiv_opcode;
  wire [3:0] sel_alu_opcode, sel_rd_source;
  wire [4:0] rd_addr, rs1_addr, rs2_addr;
  wire [6:0] funct7, opcode;
  wire [31:0] Addr, ALU_out, B_immediate, byte_sign_extended, byte_zero_extended, cache_1_data_out,
       halfword_sign_extended, halfword_zero_extended, I_immediate_Sign, I_immediate_Unsign, J_immediate,
       MulDiv_out, multiplexer_1_out, multiplexer_2_out, multiplexer_4_out, multiplexer_5_out,
       multiplexer_6_out, Next_PC, PC_4, PC_updated, Register_bank_r1, rs2_out, S_immediate, U_immediate,
       word_in;

  and and_1 (pipelined_fetch, execute, sel_IR_store);
  Multiplexer #(.width(32)) multiplexer_1 (.in0(PC_out), .in1(Next_PC), .out(multiplexer_1_out), .sel(pipelined_fetch));
  Input_data_selector input_data_selector_1 (
    .Address_2(Addr[1:0]), .Data_In(Data_in), .Word(word_in), .byte_zero_extended(byte_zero_extended),
    .halfword_zero_extended(halfword_zero_extended), .byte_sign_extended(byte_sign_extended),
    .halfword_sign_extended(halfword_sign_extended));
  cache cache_1 (
    .pipelined_fetch(pipelined_fetch), .replace_or_update(sel_IR_store), .clear(1'b0), .addr_rd(PC_out),
    .addr_upd(multiplexer_1_out), .Data_In(word_in), .In_Cache(in_cache), .Data_Out(cache_1_data_out));
  Instruction_splitter instruction_splitter_1 (
    .Instruction_Code(cache_1_data_out), .J_immediate(J_immediate), .B_immediate(B_immediate),
    .opcode(opcode), .rd(rd_addr), .funct3(funct3), .rs1(rs1_addr), .rs2(rs2_addr), .funct7(funct7),
    .S_immediate(S_immediate), .I_immediate_Unsigned(I_immediate_Unsign),
    .I_immediate_Signed(I_immediate_Sign), .U_immediate(U_immediate));
  Multiplexer #(.width(32)) multiplexer_2 (.in0(Next_PC), .in1(Start_Addr_in), .out(multiplexer_2_out), .sel(Reset_in));
  Register #(.width(32)) PC (.D(multiplexer_2_out), .en(not_1_out), .Q(PC_out), .clk(clock_1_out));  // open: clr
  not not_1 (not_1_out, hold_in);
  Clock clock_1 (.out(clock_1_out));
  Multiplexer #(.select(2), .width(32)) multiplexer_3 (
    .in0(PC_out), .in1(PC_4), .in2(ALU_out), .in3(PC_updated), .out(Next_PC), .sel(sel_PC_source));
  Multiplexer #(.select(2), .width(32)) multiplexer_4 (
    .in0(J_immediate), .in1(B_immediate), .in2(U_immediate), .in3(U_immediate), .out(multiplexer_4_out),
    .sel(sel_PC_increment));
  Adder #(.width(32)) adder_1 (.a(multiplexer_4_out), .b(PC_out), .out(PC_updated));  // open: cin, cout
  Adder #(.width(32)) adder_2 (.a(32'h4), .b(PC_out), .out(PC_4));  // open: cin, cout
  Multiplexer #(.select(4), .width(32)) multiplexer_5 (
    .in0(ALU_out), .in1(U_immediate), .in2(byte_sign_extended), .in3(byte_zero_extended),
    .in4(halfword_sign_extended), .in5(halfword_zero_extended), .in6(PC_updated), .in7(word_in), .in8(PC_4),
    .in9(MulDiv_out), .out(multiplexer_5_out), .sel(sel_rd_source));  // open: in10, in11, in12, in13, in14, in15
  nor nor_1 (nor_1_out, Reset_in, hold_in);
  Register_bank Register_bank (
    .AR2(rs2_addr), .Data_In(multiplexer_5_out), .AR1(rs1_addr), .RegWr(sel_reg_write_enable), .AW(rd_addr),
    .R2(rs2_out), .R1(Register_bank_r1));
  and and_2 (fetch, nor_1_out, ~in_cache);  // AND_Gate
  and and_3 (execute, nor_1_out, in_cache);
  multiplied_divider Mul_Div (
    .A(Register_bank_r1), .B(rs2_out), .opcode(sel_muldiv_opcode), .muldiv_out(MulDiv_out),
    .div_by_zero(div_by_zero));
  Multiplexer #(.select(2), .width(32)) multiplexer_6 (
    .in0(rs2_out), .in1(I_immediate_Sign), .in2(I_immediate_Unsign), .in3(S_immediate),
    .out(multiplexer_6_out), .sel(sel_B_source));
  ALU Arith_Logic_Unit (
    .A(Register_bank_r1), .B(multiplexer_6_out), .operation_code(sel_alu_opcode), .L(A_B),
    .Signed(A_B_signed), .Unsigned(A_B_unsigned), .Result(ALU_out));
  Instruction_decoder instruction_decoder_1 (
    .A_B_unsigned(A_B_unsigned), .div_by_zero(div_by_zero), .A_B(A_B), .A_B_signed(A_B_signed),
    .execute(execute), .fetch(fetch), .funct3(funct3), .I_immediate(I_immediate_Unsign[11:0]),
    .opcode(opcode), .funct7(funct7), .halt(unsupported_instruction), .sel_rd_source(sel_rd_source),
    .sel_reg_write_enable(sel_reg_write_enable), .sel_B_source(sel_B_source),
    .operation_code(sel_alu_opcode), .sel_PC_increment(sel_PC_increment), .sel_PC_source(sel_PC_source),
    .sel_IR_store(sel_IR_store), .sel_address_source(sel_address_source), .MemRead(MemRead),
    .MemWrite(MemWrite), .sel_muldiv_opcode(sel_muldiv_opcode), .sel_halfword_out(sel_halfword_out),
    .sel_byte_out(sel_byte_out));
  Multiplexer #(.width(32)) multiplexer_7 (.in0(ALU_out), .in1(Next_PC), .out(Addr), .sel(sel_address_source));
  assign Address = or_1_out ? {Addr[31:2], 2'b00} : 32'bz;  // Controlled_Buffer controlled_buffer_1
  or or_1 (or_1_out, MemRead, MemWrite);
  Output_data_composer output_data_composer_1 (
    .Address_2(Addr[1:0]), .Sel({sel_byte_out, sel_halfword_out}), .New_data(rs2_out), .Old_data(Data_in),
    .OutputEnable(MemWrite), .Data_out(Data_out));

  // Other names for the same wires on the sheet: PC[31:0] = PC_out; unsupported_inst_out = unsupported_instruction

  // Notes on the sheet:
  //   Address circuits
  //   Data path
  //   Control
endmodule

module Register_bank (
  input  RegWr,
  input  [4:0] AW,
  input  [31:0] Data_In,
  input  [4:0] AR1,
  input  [4:0] AR2,
  output [31:0] R1,
  output [31:0] R2
);

  wire clock_1_out, clock_2_out, clock_3_out, clock_4_out, clock_5_out, clock_6_out, clock_7_out,
       clock_8_out, clock_9_out, clock_10_out, clock_11_out, clock_12_out, clock_13_out, clock_14_out,
       clock_15_out, clock_16_out, clock_17_out, clock_18_out, clock_19_out, clock_20_out, clock_21_out,
       clock_22_out, clock_23_out, clock_24_out, clock_25_out, clock_26_out, clock_27_out, clock_28_out,
       clock_29_out, clock_30_out, clock_31_out;
  wire [3:0] decoder_1_out0, decoder_1_out4, decoder_1_out8, decoder_1_out12, decoder_1_out16,
       decoder_1_out20, decoder_1_out24, decoder_1_out28;
  wire [31:0] o1, o2, o3, o4, o5, o6, o7, o8, o9, o10, o11, o12, o13, o14, o15, o16, o17, o18, o19, o20, o21,
       o22, o23, o24, o25, o26, o27, o28, o29, o30, o31;

  Clock clock_1 (.out(clock_1_out));
  Clock clock_2 (.out(clock_2_out));
  Clock clock_3 (.out(clock_3_out));
  Register #(.width(32)) x1_ra (.D(Data_In), .en(decoder_1_out0[1]), .Q(o1), .clk(clock_1_out), .clr(1'b0));
  Register #(.width(32)) x2_sp (.D(Data_In), .en(decoder_1_out0[2]), .Q(o2), .clk(clock_2_out), .clr(1'b0));
  Register #(.width(32)) x3_gp (.D(Data_In), .en(decoder_1_out0[3]), .Q(o3), .clk(clock_3_out), .clr(1'b0));
  Clock clock_4 (.out(clock_4_out));
  Clock clock_5 (.out(clock_5_out));
  Clock clock_6 (.out(clock_6_out));
  Clock clock_7 (.out(clock_7_out));
  Multiplexer #(.select(5), .width(32)) multiplexer_1 (
    .in0({32{1'b0}}), .in1(o1), .in2(o2), .in3(o3), .in4(o4), .in5(o5), .in6(o6), .in7(o7), .in8(o8),
    .in9(o9), .in10(o10), .in11(o11), .in12(o12), .in13(o13), .in14(o14), .in15(o15), .in16(o16), .in17(o17),
    .in18(o18), .in19(o19), .in20(o20), .in21(o21), .in22(o22), .in23(o23), .in24(o24), .in25(o25),
    .in26(o26), .in27(o27), .in28(o28), .in29(o29), .in30(o30), .in31(o31), .out(R1), .sel(AR1));
  Register #(.width(32)) x4_tp (.D(Data_In), .en(decoder_1_out4[0]), .Q(o4), .clk(clock_4_out), .clr(1'b0));
  Register #(.width(32)) x5_t0 (.D(Data_In), .en(decoder_1_out4[1]), .Q(o5), .clk(clock_5_out), .clr(1'b0));
  Register #(.width(32)) x6_t1 (.D(Data_In), .en(decoder_1_out4[2]), .Q(o6), .clk(clock_6_out), .clr(1'b0));
  Register #(.width(32)) x7_t2 (.D(Data_In), .en(decoder_1_out4[3]), .Q(o7), .clk(clock_7_out), .clr(1'b0));
  Decoder #(.select(5)) decoder_1 (
    .out0(decoder_1_out0[0]), .out1(decoder_1_out0[1]), .out2(decoder_1_out0[2]), .out3(decoder_1_out0[3]),
    .out4(decoder_1_out4[0]), .out5(decoder_1_out4[1]), .out6(decoder_1_out4[2]), .out7(decoder_1_out4[3]),
    .out8(decoder_1_out8[0]), .out9(decoder_1_out8[1]), .out10(decoder_1_out8[2]), .out11(decoder_1_out8[3]),
    .out12(decoder_1_out12[0]), .out13(decoder_1_out12[1]), .out14(decoder_1_out12[2]),
    .out15(decoder_1_out12[3]), .out16(decoder_1_out16[0]), .out17(decoder_1_out16[1]),
    .out18(decoder_1_out16[2]), .out19(decoder_1_out16[3]), .out20(decoder_1_out20[0]),
    .out21(decoder_1_out20[1]), .out22(decoder_1_out20[2]), .out23(decoder_1_out20[3]),
    .out24(decoder_1_out24[0]), .out25(decoder_1_out24[1]), .out26(decoder_1_out24[2]),
    .out27(decoder_1_out24[3]), .out28(decoder_1_out28[0]), .out29(decoder_1_out28[1]),
    .out30(decoder_1_out28[2]), .out31(decoder_1_out28[3]), .sel(AW), .en(RegWr));
  Clock clock_8 (.out(clock_8_out));
  Clock clock_9 (.out(clock_9_out));
  Clock clock_10 (.out(clock_10_out));
  Clock clock_11 (.out(clock_11_out));
  Register #(.width(32)) x8_s0_fp (.D(Data_In), .en(decoder_1_out8[0]), .Q(o8), .clk(clock_8_out), .clr(1'b0));
  Register #(.width(32)) x9_s1 (.D(Data_In), .en(decoder_1_out8[1]), .Q(o9), .clk(clock_9_out), .clr(1'b0));
  Register #(.width(32)) x10_a0 (.D(Data_In), .en(decoder_1_out8[2]), .Q(o10), .clk(clock_10_out), .clr(1'b0));
  Register #(.width(32)) x11_a1 (.D(Data_In), .en(decoder_1_out8[3]), .Q(o11), .clk(clock_11_out), .clr(1'b0));
  Clock clock_12 (.out(clock_12_out));
  Clock clock_13 (.out(clock_13_out));
  Clock clock_14 (.out(clock_14_out));
  Clock clock_15 (.out(clock_15_out));
  Register #(.width(32)) x12_a2 (.D(Data_In), .en(decoder_1_out12[0]), .Q(o12), .clk(clock_12_out), .clr(1'b0));
  Register #(.width(32)) x13_a3 (.D(Data_In), .en(decoder_1_out12[1]), .Q(o13), .clk(clock_13_out), .clr(1'b0));
  Register #(.width(32)) x14_a4 (.D(Data_In), .en(decoder_1_out12[2]), .Q(o14), .clk(clock_14_out), .clr(1'b0));
  Register #(.width(32)) x15_a5 (.D(Data_In), .en(decoder_1_out12[3]), .Q(o15), .clk(clock_15_out), .clr(1'b0));
  Clock clock_16 (.out(clock_16_out));
  Clock clock_17 (.out(clock_17_out));
  Clock clock_18 (.out(clock_18_out));
  Clock clock_19 (.out(clock_19_out));
  Register #(.width(32)) x16_a6 (.D(Data_In), .en(decoder_1_out16[0]), .Q(o16), .clk(clock_16_out), .clr(1'b0));
  Register #(.width(32)) x17_a7 (.D(Data_In), .en(decoder_1_out16[1]), .Q(o17), .clk(clock_17_out), .clr(1'b0));
  Register #(.width(32)) x18_s2 (.D(Data_In), .en(decoder_1_out16[2]), .Q(o18), .clk(clock_18_out), .clr(1'b0));
  Register #(.width(32)) x19_s3 (.D(Data_In), .en(decoder_1_out16[3]), .Q(o19), .clk(clock_19_out), .clr(1'b0));
  Register #(.width(32)) x20_s4 (.D(Data_In), .en(decoder_1_out20[0]), .Q(o20), .clk(clock_20_out), .clr(1'b0));
  Clock clock_20 (.out(clock_20_out));
  Register #(.width(32)) x21_s5 (.D(Data_In), .en(decoder_1_out20[1]), .Q(o21), .clk(clock_21_out), .clr(1'b0));
  Clock clock_21 (.out(clock_21_out));
  Register #(.width(32)) x22_s6 (.D(Data_In), .en(decoder_1_out20[2]), .Q(o22), .clk(clock_22_out), .clr(1'b0));
  Clock clock_22 (.out(clock_22_out));
  Register #(.width(32)) x23_s7 (.D(Data_In), .en(decoder_1_out20[3]), .Q(o23), .clk(clock_23_out), .clr(1'b0));
  Clock clock_23 (.out(clock_23_out));
  Register #(.width(32)) x24_s8 (.D(Data_In), .en(decoder_1_out24[0]), .Q(o24), .clk(clock_24_out), .clr(1'b0));
  Clock clock_24 (.out(clock_24_out));
  Register #(.width(32)) x25_s9 (.D(Data_In), .en(decoder_1_out24[1]), .Q(o25), .clk(clock_25_out), .clr(1'b0));
  Clock clock_25 (.out(clock_25_out));
  Register #(.width(32)) x26_s10 (.D(Data_In), .en(decoder_1_out24[2]), .Q(o26), .clk(clock_26_out), .clr(1'b0));
  Clock clock_26 (.out(clock_26_out));
  Register #(.width(32)) x27_s11 (.D(Data_In), .en(decoder_1_out24[3]), .Q(o27), .clk(clock_27_out), .clr(1'b0));
  Clock clock_27 (.out(clock_27_out));
  Multiplexer #(.select(5), .width(32)) multiplexer_2 (
    .in0({32{1'b0}}), .in1(o1), .in2(o2), .in3(o3), .in4(o4), .in5(o5), .in6(o6), .in7(o7), .in8(o8),
    .in9(o9), .in10(o10), .in11(o11), .in12(o12), .in13(o13), .in14(o14), .in15(o15), .in16(o16), .in17(o17),
    .in18(o18), .in19(o19), .in20(o20), .in21(o21), .in22(o22), .in23(o23), .in24(o24), .in25(o25),
    .in26(o26), .in27(o27), .in28(o28), .in29(o29), .in30(o30), .in31(o31), .out(R2), .sel(AR2));
  Register #(.width(32)) x28_t3 (.D(Data_In), .en(decoder_1_out28[0]), .Q(o28), .clk(clock_28_out), .clr(1'b0));
  Clock clock_28 (.out(clock_28_out));
  Register #(.width(32)) x29_t4 (.D(Data_In), .en(decoder_1_out28[1]), .Q(o29), .clk(clock_29_out), .clr(1'b0));
  Clock clock_29 (.out(clock_29_out));
  Register #(.width(32)) x30_t5 (.D(Data_In), .en(decoder_1_out28[2]), .Q(o30), .clk(clock_30_out), .clr(1'b0));
  Clock clock_30 (.out(clock_30_out));
  Register #(.width(32)) x31_t6 (.D(Data_In), .en(decoder_1_out28[3]), .Q(o31), .clk(clock_31_out), .clr(1'b0));
  Clock clock_31 (.out(clock_31_out));

  // Other names for the same wires on the sheet: DI[31:0] = Data_In

  // Notes on the sheet:
  //   x0 (zero)
endmodule

module ALU (
  input  [3:0] operation_code,
  input  [31:0] A,
  input  [31:0] B,
  output L,
  output Signed,
  output Unsigned,
  output [31:0] Result
);

  wire [31:0] adder_1_out, and_1_out, or_1_out, shifter_1_out, shifter_2_out, shifter_3_out,
       subtractor_1_out, xor_1_out;

  assign and_1_out = A & B;  // AND_Gate and_1, 32 bits wide
  assign or_1_out = A | B;  // OR_Gate or_1, 32 bits wide
  Adder #(.width(32)) adder_1 (.a(A), .b(B), .out(adder_1_out), .cin(1'b0));  // open: cout
  Comparator #(.width(32)) comparator_1 (.a(A), .b(B), .eq(L), .lt(Signed));  // open: gt
  Comparator #(.mode("unsigned"), .width(32)) comparator_2 (.a(A), .b(B), .lt(Unsigned));  // open: gt, eq
  Subtractor #(.width(32)) subtractor_1 (.a(A), .b(B), .out(subtractor_1_out), .bin(1'b0));  // open: bout
  assign xor_1_out = A ^ B;  // XOR_Gate xor_1, 32 bits wide
  Shifter #(.width(32)) shifter_1 (.in(A), .\dist (B[4:0]), .out(shifter_1_out));
  Shifter #(.shift("lr"), .width(32)) shifter_2 (.in(A), .\dist (B[4:0]), .out(shifter_2_out));
  Shifter #(.shift("ar"), .width(32)) shifter_3 (.in(A), .\dist (B[4:0]), .out(shifter_3_out));
  Multiplexer #(.select(4), .width(32)) multiplexer_1 (
    .in0(adder_1_out), .in1(shifter_1_out), .in2({{31{1'b0}}, Signed}), .in3({{31{1'b0}}, Unsigned}),
    .in4(xor_1_out), .in5(shifter_2_out), .in6(or_1_out), .in7(and_1_out), .in8(subtractor_1_out),
    .in13(shifter_3_out), .out(Result), .sel(operation_code));  // open: in9, in10, in11, in12, in14, in15

  // Notes on the sheet:
  //   Unsigned
  //   operation code = funct7[5]|funct3[2:0]
endmodule

module multiplied_divider (
  input  [31:0] A,
  input  [31:0] B,
  input  [2:0] opcode,
  output [31:0] muldiv_out,
  output div_by_zero
);

  wire and_1_out, and_2_out, nor_1_out, xor_1_out;
  wire [31:0] adder_1_out, divider_1_out, divider_1_rem, divider_2_out, divider_2_rem, multiplexer_1_out,
       multiplexer_2_out, multiplexer_3_out, multiplexer_4_out, multiplexer_5_out, multiplexer_6_out,
       multiplier_1_cout, multiplier_1_out, multiplier_2_out, multiplier_3_out, negator_1_out, negator_2_out,
       negator_3_out, negator_4_out;

  and and_1 (and_1_out, opcode[0], ~opcode[1], opcode[2]);  // AND_Gate
  Multiplexer #(.width(32)) multiplexer_1 (.in0({32{1'b0}}), .in1({32{1'b1}}), .out(multiplexer_1_out), .sel(A[31]));
  Multiplexer #(.width(32)) multiplexer_2 (
    .in0({32{1'b0}}), .in1({32{1'b1}}), .out(multiplexer_2_out), .sel(and_2_out));
  and and_2 (and_2_out, ~and_1_out, B[31]);  // AND_Gate
  Negator #(.width(32)) negator_1 (.in(A), .out(negator_1_out));
  Negator #(.width(32)) negator_2 (.in(B), .out(negator_2_out));
  Multiplexer #(.width(32)) multiplexer_3 (.in0(A), .in1(negator_1_out), .out(multiplexer_3_out), .sel(A[31]));
  Multiplexer #(.width(32)) multiplexer_4 (.in0(B), .in1(negator_2_out), .out(multiplexer_4_out), .sel(B[31]));
  Multiplier #(.width(32)) multiplier_1 (.a(A), .b(B), .out(multiplier_1_out), .cout(multiplier_1_cout));  // open: cin
  Multiplier #(.width(32)) multiplier_2 (
    .a(multiplexer_1_out), .b(B), .out(multiplier_2_out), .cin(multiplier_1_cout));  // open: cout
  Multiplier #(.width(32)) multiplier_3 (.a(A), .b(multiplexer_2_out), .out(multiplier_3_out));  // open: cin, cout
  Divider #(.width(32)) divider_1 (
    .a(multiplexer_3_out), .b(multiplexer_4_out), .out(divider_1_out), .rem(divider_1_rem));  // open: upper
  Divider #(.width(32)) divider_2 (.a(A), .b(B), .out(divider_2_out), .rem(divider_2_rem));  // open: upper
  xor xor_1 (xor_1_out, B[31], A[31]);
  Negator #(.width(32)) negator_3 (.in(divider_1_out), .out(negator_3_out));
  Negator #(.width(32)) negator_4 (.in(divider_1_rem), .out(negator_4_out));
  Adder #(.width(32)) adder_1 (.a(multiplier_2_out), .b(multiplier_3_out), .out(adder_1_out));  // open: cin, cout
  Multiplexer #(.width(32)) multiplexer_5 (
    .in0(divider_1_out), .in1(negator_3_out), .out(multiplexer_5_out), .sel(xor_1_out));
  Multiplexer #(.width(32)) multiplexer_6 (
    .in0(divider_1_rem), .in1(negator_4_out), .out(multiplexer_6_out), .sel(A[31]));
  Multiplexer #(.select(3), .width(32)) multiplexer_7 (
    .in0(multiplier_1_out), .in1(adder_1_out), .in2(adder_1_out), .in3(multiplier_1_cout),
    .in4(multiplexer_5_out), .in5(divider_2_out), .in6(multiplexer_6_out), .in7(divider_2_rem),
    .out(muldiv_out), .sel(opcode));
  nor nor_1 (nor_1_out, B[0], B[1], B[2], B[3], B[4], B[5], B[6], B[7], B[8], B[9], B[10], B[11], B[12], B[13], B[14], B[15], B[16], B[17], B[18], B[19], B[20], B[21], B[22], B[23], B[24], B[25], B[26], B[27], B[28], B[29], B[30], B[31]);
  and and_3 (div_by_zero, nor_1_out, opcode[2]);

  // Other names for the same wires on the sheet: dividend_sign = A[31]; division = opcode[2]

  // Notes on the sheet:
  //   same as funct3 code in muldiv
  //   A
  //   B
  //   mulhsu
  //   Multiplier
  //   Divider
  //   A<0
  //   B<0
  //   abs(A)
  //   abs(B)
  //   mul
  //   mulhu
  //   mulh/mulhsu
  //   div
  //   rem
  //   divu
  //   remu
endmodule

// Instruction split
module Instruction_splitter (
  input  [31:0] Instruction_Code,
  output [6:0] opcode,
  output [4:0] rd,
  output [2:0] funct3,
  output [4:0] rs1,
  output [31:0] I_immediate_Signed,
  output [31:0] J_immediate,
  output [4:0] rs2,
  output [6:0] funct7,
  output [31:0] S_immediate,
  output [31:0] U_immediate,
  output [31:0] B_immediate,
  output [31:0] I_immediate_Unsigned
);


  assign B_immediate = {{20{Instruction_Code[31]}}, Instruction_Code[7], Instruction_Code[30:25], Instruction_Code[11:8], 1'b0};
  assign funct3 = Instruction_Code[14:12];
  assign funct7 = Instruction_Code[31:25];
  assign I_immediate_Signed = {{21{Instruction_Code[31]}}, Instruction_Code[30:20]};
  assign I_immediate_Unsigned = {{20{1'b0}}, Instruction_Code[31:20]};
  assign J_immediate = {{12{Instruction_Code[31]}}, Instruction_Code[19:12], Instruction_Code[20], Instruction_Code[30:21], 1'b0};
  assign opcode = Instruction_Code[6:0];
  assign rd = Instruction_Code[11:7];
  assign rs1 = Instruction_Code[19:15];
  assign rs2 = Instruction_Code[24:20];
  assign S_immediate = {{21{Instruction_Code[31]}}, Instruction_Code[30:25], Instruction_Code[11:7]};
  assign U_immediate = {Instruction_Code[31:12], {12{1'b0}}};

  // Notes on the sheet:
  //   R-type
endmodule

// Instruction decoder
module Instruction_decoder (
  input  [6:0] funct7,
  input  [2:0] funct3,
  input  [6:0] opcode,
  input  execute,
  input  fetch,
  input  A_B,
  input  A_B_signed,
  input  A_B_unsigned,
  input  div_by_zero,
  input  [11:0] I_immediate,
  output [1:0] sel_PC_increment,
  output [1:0] sel_PC_source,
  output sel_IR_store,
  output sel_address_source,
  output MemRead,
  output sel_halfword_out,
  output MemWrite,
  output sel_byte_out,
  output [3:0] operation_code,
  output [2:0] sel_muldiv_opcode,
  output [1:0] sel_B_source,
  output [3:0] sel_rd_source,
  output sel_reg_write_enable,
  output halt
);

  wire add, addi, \and , and_11_out, and_16_out, and_17_out, and_18_out, and_19_out, and_20_out, and_21_out,
       and_22_out, and_23_out, and_30_out, and_31_out, andi, arith, arith_imm, beq, bge, bgeu, blt, bltu,
       bne, branch, decoder_7_out1, decoder_7_out5, div, divu, ebreak, ecall, funct3_0x0, funct7_0x0,
       funct7_0x1, funct7_0x20, I_imm_0x0, I_imm_0x1, jal, jalr, lb, lbu, lh, lhu, load, lui, lw, mul,
       muldiv, mulh, mulsu, mulu, nor_2_out, \or , or_2_out, or_3_out, or_6_out, or_7_out, or_8_out,
       or_9_out, ori, rem, remu, sll, slli, slt, slti, sltiu, sltu, sra, srai, srl, srli, sub, sw, system,
       unsupported_instruction, \xor , xori;
  wire [3:3] multiplexer_2_out;
  wire [6:0] multiplexer_1_out;

  Multiplexer #(.width(7)) multiplexer_1 (.in0({7{1'b0}}), .in1(opcode), .out(multiplexer_1_out), .sel(execute));
  and and_1 (funct7_0x1, funct7[0], ~funct7[1], ~funct7[2], ~funct7[3], ~funct7[4], ~funct7[5], ~funct7[6]);  // AND_Gate
  and and_2 (funct7_0x0, ~funct7[0], ~funct7[1], ~funct7[2], ~funct7[3], ~funct7[4], ~funct7[5], ~funct7[6]);  // AND_Gate
  and and_3 (funct7_0x20, ~funct7[0], ~funct7[1], ~funct7[2], ~funct7[3], ~funct7[4], funct7[5], ~funct7[6]);  // AND_Gate
  nor nor_1 (funct3_0x0, funct3[0], funct3[1], funct3[2]);
  and and_4 (arith, multiplexer_1_out[0], multiplexer_1_out[1], ~multiplexer_1_out[2], ~multiplexer_1_out[3], multiplexer_1_out[4], multiplexer_1_out[5], ~multiplexer_1_out[6]);  // AND_Gate
  and and_5 (arith_imm, multiplexer_1_out[0], multiplexer_1_out[1], ~multiplexer_1_out[2], ~multiplexer_1_out[3], multiplexer_1_out[4], ~multiplexer_1_out[5], ~multiplexer_1_out[6]);  // AND_Gate
  and and_6 (load, multiplexer_1_out[0], multiplexer_1_out[1], ~multiplexer_1_out[2], ~multiplexer_1_out[3], ~multiplexer_1_out[4], ~multiplexer_1_out[5], ~multiplexer_1_out[6]);  // AND_Gate
  and and_7 (MemWrite, multiplexer_1_out[0], multiplexer_1_out[1], ~multiplexer_1_out[2], ~multiplexer_1_out[3], ~multiplexer_1_out[4], multiplexer_1_out[5], ~multiplexer_1_out[6]);  // AND_Gate
  and and_8 (branch, multiplexer_1_out[0], multiplexer_1_out[1], ~multiplexer_1_out[2], ~multiplexer_1_out[3], ~multiplexer_1_out[4], multiplexer_1_out[5], multiplexer_1_out[6]);  // AND_Gate
  and and_9 (lui, multiplexer_1_out[0], multiplexer_1_out[1], multiplexer_1_out[2], ~multiplexer_1_out[3], multiplexer_1_out[4], multiplexer_1_out[5], ~multiplexer_1_out[6]);  // AND_Gate
  and and_10 (jal, multiplexer_1_out[0], multiplexer_1_out[1], multiplexer_1_out[2], multiplexer_1_out[3], ~multiplexer_1_out[4], multiplexer_1_out[5], multiplexer_1_out[6]);  // AND_Gate
  and and_11 (and_11_out, multiplexer_1_out[0], multiplexer_1_out[1], multiplexer_1_out[2], ~multiplexer_1_out[3], ~multiplexer_1_out[4], multiplexer_1_out[5], multiplexer_1_out[6]);  // AND_Gate
  and and_12 (system, multiplexer_1_out[0], multiplexer_1_out[1], ~multiplexer_1_out[2], ~multiplexer_1_out[3], multiplexer_1_out[4], multiplexer_1_out[5], multiplexer_1_out[6]);  // AND_Gate
  and and_13 (sel_PC_increment[1], multiplexer_1_out[0], multiplexer_1_out[1], multiplexer_1_out[2], ~multiplexer_1_out[3], multiplexer_1_out[4], ~multiplexer_1_out[5], ~multiplexer_1_out[6]);  // AND_Gate
  and and_14 (jalr, funct3_0x0, and_11_out);
  Decoder #(.select(3)) decoder_1 (
    .out0(lb), .out1(lh), .out2(lw), .out4(lbu), .out5(lhu), .sel(funct3), .en(load));  // open: out3, out6, out7
  Decoder #(.select(3)) decoder_2 (
    .out0(beq), .out1(bne), .out4(blt), .out5(bge), .out6(bltu), .out7(bgeu), .sel(funct3), .en(branch));  // open: out2, out3
  Decoder #(.select(3)) decoder_3 (
    .out0(mul), .out1(mulh), .out2(mulsu), .out3(mulu), .out4(div), .out5(divu), .out6(rem), .out7(remu),
    .sel(funct3), .en(muldiv));
  and and_15 (muldiv, arith, funct7_0x1);
  Decoder #(.select(3)) decoder_4 (
    .out0(add), .out1(sll), .out2(slt), .out3(sltu), .out4(\xor ), .out5(srl), .out6(\or ), .out7(\and ),
    .sel(funct3), .en(and_16_out));
  and and_16 (and_16_out, arith, funct7_0x0);
  Decoder #(.select(3)) decoder_5 (
    .out0(sub), .out5(sra), .sel(funct3), .en(and_17_out));  // open: out1, out2, out3, out4, out6, out7
  and and_17 (and_17_out, arith, funct7_0x20);
  and and_18 (and_18_out, beq, A_B);
  and and_19 (and_19_out, ~A_B, bne);  // AND_Gate
  and and_20 (and_20_out, blt, A_B_signed);
  and and_21 (and_21_out, ~A_B_signed, bge);  // AND_Gate
  and and_22 (and_22_out, bltu, A_B_unsigned);
  and and_23 (and_23_out, ~A_B_unsigned, bgeu);  // AND_Gate
  Decoder #(.select(3)) decoder_6 (
    .out0(sel_byte_out), .out1(sel_halfword_out), .out2(sw), .sel(funct3), .en(MemWrite));  // open: out3, out4, out5, out6, out7
  or or_1 (sel_PC_increment[0], and_18_out, and_19_out, and_20_out, and_21_out, and_22_out, and_23_out);
  Decoder #(.select(3)) decoder_7 (
    .out0(addi), .out1(decoder_7_out1), .out2(slti), .out3(sltiu), .out4(xori), .out5(decoder_7_out5),
    .out6(ori), .out7(andi), .sel(funct3), .en(arith_imm));
  and and_24 (slli, decoder_7_out1, funct7_0x0);
  and and_25 (srai, decoder_7_out5, funct7_0x20);
  and and_26 (srli, decoder_7_out5, funct7_0x0);
  Comparator #(.mode("unsigned"), .width(12)) comparator_1 (
    .a(I_immediate), .b({12{1'b0}}), .eq(I_imm_0x0));  // open: gt, lt
  Comparator #(.mode("unsigned"), .width(12)) comparator_2 (
    .a(I_immediate), .b(12'h1), .eq(I_imm_0x1));  // open: gt, lt
  and and_27 (ebreak, I_imm_0x1, system, funct3_0x0);
  and and_28 (ecall, system, funct3_0x0, I_imm_0x0);
  or or_2 (or_2_out, beq, bne, blt, bge, bltu, bgeu, sel_byte_out, sel_halfword_out, sw, lh, lb, lhu, lw, slli, lbu, srai, srli, sltiu, addi, andi, slti, ori, add, xori, slt, sll, \xor , sltu, \or , srl, \and , sub);
  nor nor_2 (nor_2_out, load, MemWrite);
  or or_3 (or_3_out, sra, ebreak, ecall, muldiv, jalr, lui, jal, sel_PC_increment[1], or_2_out);
  and and_29 (unsupported_instruction, ~or_3_out, execute);  // AND_Gate
  or or_4 (sel_address_source, nor_2_out, fetch);
  and and_30 (and_30_out, muldiv, funct3[2], div_by_zero);
  or or_5 (halt, unsupported_instruction, and_30_out, ebreak);
  or or_6 (or_6_out, sel_PC_increment[0], jal);
  and and_31 (and_31_out, srai, arith_imm);
  Multiplexer multiplexer_2 (.in0(and_31_out), .in1(funct7_0x20), .out(multiplexer_2_out[3]), .sel(arith));
  Priority_Encoder #(.select(2)) priority_encoder_1 (
    .in0(1'b1), .in1(execute), .in2(jalr), .in3(or_6_out), .out(sel_PC_source));  // open: gs, en_out, en_in
  Multiplexer #(.width(4)) multiplexer_3 (
    .in0(4'b0000), .in1({multiplexer_2_out[3], funct3}), .out(operation_code), .sel(or_7_out));
  or or_7 (or_7_out, arith, arith_imm);
  or or_8 (or_8_out, load, arith_imm, jalr);
  or or_9 (or_9_out, jal, jalr);
  or or_10 (MemRead, sel_address_source, load, MemWrite);
  Priority_Encoder #(.select(2)) priority_encoder_2 (
    .in0(1'b1), .in1(or_8_out), .in2(sltiu), .in3(MemWrite), .out(sel_B_source));  // open: gs, en_out, en_in
  Priority_Encoder #(.select(4)) priority_encoder_3 (
    .in0(1'b1), .in1(lui), .in2(lb), .in3(lbu), .in4(lh), .in5(lhu), .in6(sel_PC_increment[1]), .in7(lw),
    .in8(or_9_out), .in9(muldiv), .out(sel_rd_source));  // open: in10, in11, in12, in13, in14, in15, gs, en_out, en_in
  or or_11 (sel_reg_write_enable, sel_PC_increment[1], arith_imm, arith, load, jalr, lui, jal, muldiv);

  assign sel_IR_store = sel_address_source;
  assign sel_muldiv_opcode = funct3;

  // Other names for the same wires on the sheet: do_fetch = sel_address_source; I_imm[11:0] = I_immediate;
  //   sb = sel_byte_out; do_branch = sel_PC_increment[0]; auipc = sel_PC_increment[1]; sh = sel_halfword_out;
  //   store = MemWrite

  // Notes on the sheet:
  //   Arithmetic instrucitons
  //   Load instructions
  //   Branch instructions
  //   Condition processing
  //   multiplication and division
  //   Store instructions
  //   Arithmetic instrucitons with immediate operand
  //   system instructions (t.b.d.)
  //   illegal instruction detection
  //   00 = PC+J-immediate (jal)
  //   01 = PC+B-immediate
  //   1x = PC+U-immediate
  //   01 = PC+4
  //   10 = ALU-out
  //   00 = PC  (PC is unchanged)
  //   00 = rs2
  //   0000 = ALU out
  //   1000 = PC+4
  //   11 = Incremented PC (see sel-PC-increment)
  //   0=ALU out, 1=PC
  //   01 = I-immediate-sign-extended
  //   10 = I-immediate-zero-extended
  //   11 = S-immediate-sign-extended
  //   0001 = U-immediate
  //   0111 = word from memory
  //   1001 = MulDiv output
  //   0010 = byte from memory sign extended
  //   0011 = byte from memory zero extended
  //   0100 = halfword from memory sign extended
  //   0101 = halfword from memory zero extended
  //   0110 = Incremented PC (see sel-PC-increment)
endmodule

module Input_data_selector (
  input  [1:0] Address_2,
  input  [31:0] Data_In,
  output [31:0] byte_sign_extended,
  output [31:0] byte_zero_extended,
  output [31:0] halfword_sign_extended,
  output [31:0] halfword_zero_extended,
  output [31:0] Word
);

  Multiplexer #(.select(2), .width(8)) multiplexer_1 (
    .in0(Data_In[7:0]), .in1(Data_In[15:8]), .in2(Data_In[23:16]), .in3(Data_In[31:24]),
    .out({byte_sign_extended[31], byte_sign_extended[6:0]}), .sel(Address_2));
  Multiplexer #(.width(16)) multiplexer_2 (
    .in0(Data_In[15:0]), .in1(Data_In[31:16]),
    .out({halfword_sign_extended[31], halfword_sign_extended[14:0]}), .sel(Address_2[1]));

  assign byte_sign_extended[30:7] = {24{byte_sign_extended[31]}};
  assign byte_zero_extended = {{24{1'b0}}, byte_sign_extended[31], byte_sign_extended[6:0]};
  assign halfword_sign_extended[30:15] = {16{halfword_sign_extended[31]}};
  assign halfword_zero_extended = {{16{1'b0}}, halfword_sign_extended[31], halfword_sign_extended[14:0]};
  assign Word = Data_In;

  // Notes on the sheet:
  //   Data selector circuit. Picks half words and byte output based on the least significant bits of address
endmodule

module Output_data_composer (
  input  [1:0] Address_2,
  input  [1:0] Sel,
  input  [31:0] New_data,
  input  [31:0] Old_data,
  input  OutputEnable,
  output [31:0] Data_out
);

  wire decoder_1_out0, decoder_1_out1, decoder_1_out2, decoder_1_out3, decoder_2_out0, decoder_2_out1,
       multiplexer_5_out, multiplexer_10_out, multiplexer_11_out, multiplexer_12_out;
  wire [7:0] multiplexer_1_out, multiplexer_2_out, multiplexer_3_out, multiplexer_4_out, multiplexer_6_out,
       multiplexer_7_out, multiplexer_8_out, multiplexer_9_out;

  Decoder #(.enable("false"), .select(2)) decoder_1 (
    .out0(decoder_1_out0), .out1(decoder_1_out1), .out2(decoder_1_out2), .out3(decoder_1_out3),
    .sel(Address_2));
  Decoder #(.enable("false")) decoder_2 (.out0(decoder_2_out0), .out1(decoder_2_out1), .sel(Address_2[1]));
  Multiplexer #(.select(2), .width(8)) multiplexer_1 (
    .in0(New_data[7:0]), .in1(New_data[7:0]), .in2(New_data[7:0]), .in3(New_data[7:0]),
    .out(multiplexer_1_out), .sel(Sel));
  Multiplexer #(.select(2), .width(8)) multiplexer_2 (
    .in0(New_data[15:8]), .in1(New_data[15:8]), .in2(New_data[7:0]), .in3(New_data[7:0]),
    .out(multiplexer_2_out), .sel(Sel));
  Multiplexer #(.select(2), .width(8)) multiplexer_3 (
    .in0(New_data[23:16]), .in1(New_data[7:0]), .in2(New_data[7:0]), .in3(New_data[7:0]),
    .out(multiplexer_3_out), .sel(Sel));
  Multiplexer #(.select(2), .width(8)) multiplexer_4 (
    .in0(New_data[31:24]), .in1(New_data[15:8]), .in2(New_data[7:0]), .in3(New_data[7:0]),
    .out(multiplexer_4_out), .sel(Sel));
  Multiplexer #(.select(2)) multiplexer_5 (
    .in0(1'b1), .in1(decoder_2_out0), .in2(decoder_1_out0), .in3(decoder_1_out0), .out(multiplexer_5_out),
    .sel(Sel));
  Multiplexer #(.width(8)) multiplexer_6 (
    .in0(Old_data[7:0]), .in1(multiplexer_1_out), .out(multiplexer_6_out), .sel(multiplexer_5_out));
  Multiplexer #(.width(8)) multiplexer_7 (
    .in0(Old_data[15:8]), .in1(multiplexer_2_out), .out(multiplexer_7_out), .sel(multiplexer_10_out));
  Multiplexer #(.width(8)) multiplexer_8 (
    .in0(Old_data[23:16]), .in1(multiplexer_3_out), .out(multiplexer_8_out), .sel(multiplexer_11_out));
  Multiplexer #(.width(8)) multiplexer_9 (
    .in0(Old_data[31:24]), .in1(multiplexer_4_out), .out(multiplexer_9_out), .sel(multiplexer_12_out));
  Multiplexer #(.select(2)) multiplexer_10 (
    .in0(1'b1), .in1(decoder_2_out0), .in2(decoder_1_out1), .in3(decoder_1_out1), .out(multiplexer_10_out),
    .sel(Sel));
  Multiplexer #(.select(2)) multiplexer_11 (
    .in0(1'b1), .in1(decoder_2_out1), .in2(decoder_1_out2), .in3(decoder_1_out2), .out(multiplexer_11_out),
    .sel(Sel));
  Multiplexer #(.select(2)) multiplexer_12 (
    .in0(1'b1), .in1(decoder_2_out1), .in2(decoder_1_out3), .in3(decoder_1_out3), .out(multiplexer_12_out),
    .sel(Sel));
  assign Data_out = OutputEnable ? {multiplexer_9_out, multiplexer_8_out, multiplexer_7_out, multiplexer_6_out} : 32'bz;  // Controlled_Buffer controlled_buffer_1

  // Notes on the sheet:
  //   Sel = 00 - word
  //   Sel = 01 - halfword
  //   Sel = 1x - byte
  //   Output data composer - replaces part of the old 32-bit memory word with new data based on the two least significant bits of address and the width of new data being written: byte, halfword, or word.
endmodule

module Videoram_for_monochrome_display (
  input  str,
  input  [4:0] Address,
  input  [31:0] Data_In,
  input  ld,
  output [31:0] L_0,
  output [31:0] L_8,
  output [31:0] L_16,
  output [31:0] L_24,
  output [31:0] L_1,
  output [31:0] L_9,
  output [31:0] L_17,
  output [31:0] L_25,
  output [31:0] L_2,
  output [31:0] L_10,
  output [31:0] L_18,
  output [31:0] L_26,
  output [31:0] L_3,
  output [31:0] L_11,
  output [31:0] L_19,
  output [31:0] L_27,
  output [31:0] L_4,
  output [31:0] L_12,
  output [31:0] L_20,
  output [31:0] L_28,
  output [31:0] L_5,
  output [31:0] L_13,
  output [31:0] L_21,
  output [31:0] L_29,
  output [31:0] L_6,
  output [31:0] L_14,
  output [31:0] L_22,
  output [31:0] L_30,
  output [31:0] L_7,
  output [31:0] L_15,
  output [31:0] L_23,
  output [31:0] L_31,
  output [31:0] Data_Out
);

  wire clock_1_out, clock_2_out, clock_3_out, clock_4_out, clock_5_out, clock_6_out, clock_7_out,
       clock_8_out, clock_9_out, clock_10_out, clock_11_out, clock_12_out, clock_13_out, clock_14_out,
       clock_15_out, clock_16_out, clock_17_out, clock_18_out, clock_19_out, clock_20_out, clock_21_out,
       clock_22_out, clock_23_out, clock_24_out, clock_25_out, clock_26_out, clock_27_out, clock_28_out,
       clock_29_out, clock_30_out, clock_31_out, clock_32_out;
  wire [3:0] decoder_1_out0, decoder_1_out4, decoder_1_out8, decoder_1_out12, decoder_1_out16,
       decoder_1_out20, decoder_1_out24, decoder_1_out28;

  Clock clock_1 (.out(clock_1_out));
  Clock clock_2 (.out(clock_2_out));
  Clock clock_3 (.out(clock_3_out));
  Clock clock_4 (.out(clock_4_out));
  Register #(.width(32)) r0 (.D(Data_In), .en(decoder_1_out0[0]), .Q(L_0), .clk(clock_1_out), .clr(1'b0));
  Register #(.width(32)) r1 (.D(Data_In), .en(decoder_1_out0[1]), .Q(L_1), .clk(clock_2_out), .clr(1'b0));
  Register #(.width(32)) r2 (.D(Data_In), .en(decoder_1_out0[2]), .Q(L_2), .clk(clock_3_out), .clr(1'b0));
  Register #(.width(32)) r3 (.D(Data_In), .en(decoder_1_out0[3]), .Q(L_3), .clk(clock_4_out), .clr(1'b0));
  Clock clock_5 (.out(clock_5_out));
  Clock clock_6 (.out(clock_6_out));
  Clock clock_7 (.out(clock_7_out));
  Clock clock_8 (.out(clock_8_out));
  Multiplexer #(.disabled("Z"), .enable("true"), .select(5), .width(32)) multiplexer_1 (
    .in0(L_0), .in1(L_1), .in2(L_2), .in3(L_3), .in4(L_4), .in5(L_5), .in6(L_6), .in7(L_7), .in8(L_8),
    .in9(L_9), .in10(L_10), .in11(L_11), .in12(L_12), .in13(L_13), .in14(L_14), .in15(L_15), .in16(L_16),
    .in17(L_17), .in18(L_18), .in19(L_19), .in20(L_20), .in21(L_21), .in22(L_22), .in23(L_23), .in24(L_24),
    .in25(L_25), .in26(L_26), .in27(L_27), .in28(L_28), .in29(L_29), .in30(L_30), .in31(L_31),
    .out(Data_Out), .sel(Address), .en(ld));
  Register #(.width(32)) r4 (.D(Data_In), .en(decoder_1_out4[0]), .Q(L_4), .clk(clock_5_out), .clr(1'b0));
  Register #(.width(32)) r5 (.D(Data_In), .en(decoder_1_out4[1]), .Q(L_5), .clk(clock_6_out), .clr(1'b0));
  Register #(.width(32)) r6 (.D(Data_In), .en(decoder_1_out4[2]), .Q(L_6), .clk(clock_7_out), .clr(1'b0));
  Register #(.width(32)) r7 (.D(Data_In), .en(decoder_1_out4[3]), .Q(L_7), .clk(clock_8_out), .clr(1'b0));
  Decoder #(.select(5)) decoder_1 (
    .out0(decoder_1_out0[0]), .out1(decoder_1_out0[1]), .out2(decoder_1_out0[2]), .out3(decoder_1_out0[3]),
    .out4(decoder_1_out4[0]), .out5(decoder_1_out4[1]), .out6(decoder_1_out4[2]), .out7(decoder_1_out4[3]),
    .out8(decoder_1_out8[0]), .out9(decoder_1_out8[1]), .out10(decoder_1_out8[2]), .out11(decoder_1_out8[3]),
    .out12(decoder_1_out12[0]), .out13(decoder_1_out12[1]), .out14(decoder_1_out12[2]),
    .out15(decoder_1_out12[3]), .out16(decoder_1_out16[0]), .out17(decoder_1_out16[1]),
    .out18(decoder_1_out16[2]), .out19(decoder_1_out16[3]), .out20(decoder_1_out20[0]),
    .out21(decoder_1_out20[1]), .out22(decoder_1_out20[2]), .out23(decoder_1_out20[3]),
    .out24(decoder_1_out24[0]), .out25(decoder_1_out24[1]), .out26(decoder_1_out24[2]),
    .out27(decoder_1_out24[3]), .out28(decoder_1_out28[0]), .out29(decoder_1_out28[1]),
    .out30(decoder_1_out28[2]), .out31(decoder_1_out28[3]), .sel(Address), .en(str));
  Clock clock_9 (.out(clock_9_out));
  Clock clock_10 (.out(clock_10_out));
  Clock clock_11 (.out(clock_11_out));
  Clock clock_12 (.out(clock_12_out));
  Register #(.width(32)) r8 (.D(Data_In), .en(decoder_1_out8[0]), .Q(L_8), .clk(clock_9_out), .clr(1'b0));
  Register #(.width(32)) r9 (.D(Data_In), .en(decoder_1_out8[1]), .Q(L_9), .clk(clock_10_out), .clr(1'b0));
  Register #(.width(32)) r10 (.D(Data_In), .en(decoder_1_out8[2]), .Q(L_10), .clk(clock_11_out), .clr(1'b0));
  Register #(.width(32)) r11 (.D(Data_In), .en(decoder_1_out8[3]), .Q(L_11), .clk(clock_12_out), .clr(1'b0));
  Clock clock_13 (.out(clock_13_out));
  Clock clock_14 (.out(clock_14_out));
  Clock clock_15 (.out(clock_15_out));
  Clock clock_16 (.out(clock_16_out));
  Register #(.width(32)) r12 (.D(Data_In), .en(decoder_1_out12[0]), .Q(L_12), .clk(clock_13_out), .clr(1'b0));
  Register #(.width(32)) r13 (.D(Data_In), .en(decoder_1_out12[1]), .Q(L_13), .clk(clock_14_out), .clr(1'b0));
  Register #(.width(32)) r14 (.D(Data_In), .en(decoder_1_out12[2]), .Q(L_14), .clk(clock_15_out), .clr(1'b0));
  Register #(.width(32)) r15 (.D(Data_In), .en(decoder_1_out12[3]), .Q(L_15), .clk(clock_16_out), .clr(1'b0));
  Clock clock_17 (.out(clock_17_out));
  Clock clock_18 (.out(clock_18_out));
  Clock clock_19 (.out(clock_19_out));
  Clock clock_20 (.out(clock_20_out));
  Register #(.width(32)) r16 (.D(Data_In), .en(decoder_1_out16[0]), .Q(L_16), .clk(clock_17_out), .clr(1'b0));
  Register #(.width(32)) r17 (.D(Data_In), .en(decoder_1_out16[1]), .Q(L_17), .clk(clock_18_out), .clr(1'b0));
  Register #(.width(32)) r18 (.D(Data_In), .en(decoder_1_out16[2]), .Q(L_18), .clk(clock_19_out), .clr(1'b0));
  Register #(.width(32)) r19 (.D(Data_In), .en(decoder_1_out16[3]), .Q(L_19), .clk(clock_20_out), .clr(1'b0));
  Register #(.width(32)) r20 (.D(Data_In), .en(decoder_1_out20[0]), .Q(L_20), .clk(clock_21_out), .clr(1'b0));
  Clock clock_21 (.out(clock_21_out));
  Register #(.width(32)) r21 (.D(Data_In), .en(decoder_1_out20[1]), .Q(L_21), .clk(clock_22_out), .clr(1'b0));
  Clock clock_22 (.out(clock_22_out));
  Register #(.width(32)) r22 (.D(Data_In), .en(decoder_1_out20[2]), .Q(L_22), .clk(clock_23_out), .clr(1'b0));
  Clock clock_23 (.out(clock_23_out));
  Register #(.width(32)) r23 (.D(Data_In), .en(decoder_1_out20[3]), .Q(L_23), .clk(clock_24_out), .clr(1'b0));
  Clock clock_24 (.out(clock_24_out));
  Register #(.width(32)) r24 (.D(Data_In), .en(decoder_1_out24[0]), .Q(L_24), .clk(clock_25_out), .clr(1'b0));
  Clock clock_25 (.out(clock_25_out));
  Register #(.width(32)) r25 (.D(Data_In), .en(decoder_1_out24[1]), .Q(L_25), .clk(clock_26_out), .clr(1'b0));
  Clock clock_26 (.out(clock_26_out));
  Register #(.width(32)) r26 (.D(Data_In), .en(decoder_1_out24[2]), .Q(L_26), .clk(clock_27_out), .clr(1'b0));
  Clock clock_27 (.out(clock_27_out));
  Register #(.width(32)) r27 (.D(Data_In), .en(decoder_1_out24[3]), .Q(L_27), .clk(clock_28_out), .clr(1'b0));
  Clock clock_28 (.out(clock_28_out));
  Register #(.width(32)) r28 (.D(Data_In), .en(decoder_1_out28[0]), .Q(L_28), .clk(clock_29_out), .clr(1'b0));
  Clock clock_29 (.out(clock_29_out));
  Register #(.width(32)) r29 (.D(Data_In), .en(decoder_1_out28[1]), .Q(L_29), .clk(clock_30_out), .clr(1'b0));
  Clock clock_30 (.out(clock_30_out));
  Register #(.width(32)) r30 (.D(Data_In), .en(decoder_1_out28[2]), .Q(L_30), .clk(clock_31_out), .clr(1'b0));
  Clock clock_31 (.out(clock_31_out));
  Register #(.width(32)) r31 (.D(Data_In), .en(decoder_1_out28[3]), .Q(L_31), .clk(clock_32_out), .clr(1'b0));
  Clock clock_32 (.out(clock_32_out));

  // Other names for the same wires on the sheet: DI[31:0] = Data_In; o0[31:0] = L_0; o1[31:0] = L_1; o2[31:0] = L_2;
  //   o3[31:0] = L_3; o4[31:0] = L_4; o5[31:0] = L_5; o6[31:0] = L_6; o7[31:0] = L_7; o8[31:0] = L_8; o9[31:0] = L_9;
  //   o10[31:0] = L_10; o11[31:0] = L_11; o12[31:0] = L_12; o13[31:0] = L_13; o14[31:0] = L_14; o15[31:0] = L_15;
  //   o16[31:0] = L_16; o17[31:0] = L_17; o18[31:0] = L_18; o19[31:0] = L_19; o20[31:0] = L_20; o21[31:0] = L_21;
  //   o22[31:0] = L_22; o23[31:0] = L_23; o24[31:0] = L_24; o25[31:0] = L_25; o26[31:0] = L_26; o27[31:0] = L_27;
  //   o28[31:0] = L_28; o29[31:0] = L_29; o30[31:0] = L_30; o31[31:0] = L_31
endmodule

module cache (
  input  pipelined_fetch,
  input  replace_or_update,
  input  clear,
  input  [31:0] addr_rd,
  input  [31:0] addr_upd,
  input  [31:0] Data_In,
  output [31:0] Data_Out,
  output In_Cache
);

  wire and_2_out, and_3_out, and_4_out, and_5_out, and_6_out, and_7_out, and_8_out, and_9_out, clock_1_out,
       clock_2_out, clock_3_out, clock_4_out, clock_5_out, clock_7_out, clock_8_out, clock_9_out,
       clock_10_out, clock_11_out, clock_12_out, clock_13_out, clock_14_out, clock_15_out, clock_16_out,
       clock_17_out, clock_18_out, clock_19_out, comparator_1_eq, comparator_2_eq, comparator_3_eq,
       comparator_4_eq, comparator_5_eq, comparator_6_eq, comparator_7_eq, comparator_8_eq, comparator_9_eq,
       decoder_1_out0, decoder_1_out1, decoder_1_out2, decoder_1_out3, decoder_1_out4, decoder_1_out5,
       decoder_1_out6, decoder_1_out7, not_1_out, priority_encoder_1_p6, priority_encoder_1_p8,
       priority_encoder_1_p9, priority_encoder_1_p10, R, rand_gen_p2;
  wire [2:0] matching_Ax, multiplexer_1_out, multiplexer_2_out, undriven;
  wire [31:0] D0_q, D1_q, D2_q, D3_q, D4_q, D5_q, D6_q, D7_q;
  wire [32:0] A0_q, A1_q, A2_q, A3_q, A4_q, A5_q, A6_q, A7_q;

  and and_1 (R, clear, clock_1_out);
  Clock clock_1 (.out(clock_1_out));
  Comparator #(.width(32)) comparator_1 (.a(addr_rd), .b(addr_upd), .eq(comparator_1_eq));  // open: gt, lt
  Register #(.width(33)) A0 (.D({1'b1, addr_upd}), .en(decoder_1_out0), .Q(A0_q), .clk(clock_2_out), .clr(R));
  Clock clock_2 (.out(clock_2_out));
  Register #(.width(32)) D0 (.D(Data_In), .en(decoder_1_out0), .Q(D0_q), .clk(clock_3_out), .clr(R));
  Clock clock_3 (.out(clock_3_out));
  and and_2 (and_2_out, In_Cache, comparator_1_eq);
  Comparator #(.width(32)) comparator_2 (.a(addr_rd), .b(A0_q[31:0]), .eq(comparator_2_eq));  // open: gt, lt
  and and_3 (and_3_out, A0_q[32], comparator_2_eq);
  assign Data_Out = and_3_out ? D0_q : 32'bz;  // Controlled_Buffer controlled_buffer_1
  Clock clock_4 (.out(clock_4_out));
  Clock clock_5 (.out(clock_5_out));
  // Random #(.width(3)) rand_gen: pin names not known; wires that end beside it: 1'b1, rand_gen_p2
  Clock clock_6 (.out(rand_gen_p2));
  Register #(.width(33)) A1 (.D({1'b1, addr_upd}), .en(decoder_1_out1), .Q(A1_q), .clk(clock_4_out), .clr(R));
  Register #(.width(32)) D1 (.D(Data_In), .en(decoder_1_out1), .Q(D1_q), .clk(clock_5_out), .clr(R));
  Multiplexer #(.width(3)) multiplexer_1 (.in0(undriven), .in1(matching_Ax), .out(multiplexer_1_out), .sel(and_2_out));
  and and_4 (and_4_out, ~and_2_out, pipelined_fetch);  // AND_Gate
  Comparator #(.width(32)) comparator_3 (.a(addr_rd), .b(A1_q[31:0]), .eq(comparator_3_eq));  // open: gt, lt
  and and_5 (and_5_out, A1_q[32], comparator_3_eq);
  assign Data_Out = and_5_out ? D1_q : 32'bz;  // Controlled_Buffer controlled_buffer_2
  Multiplexer #(.width(3)) multiplexer_2 (
    .in0(multiplexer_1_out), .in1(3'b000), .out(multiplexer_2_out), .sel(and_4_out));
  Clock clock_7 (.out(clock_7_out));
  Clock clock_8 (.out(clock_8_out));
  not not_1 (not_1_out, pipelined_fetch);
  Register #(.width(33)) A2 (.D({1'b1, addr_upd}), .en(decoder_1_out2), .Q(A2_q), .clk(clock_7_out), .clr(R));
  Register #(.width(32)) D2 (.D(Data_In), .en(decoder_1_out2), .Q(D2_q), .clk(clock_8_out), .clr(R));
  Comparator #(.width(32)) comparator_4 (.a(addr_rd), .b(A2_q[31:0]), .eq(comparator_4_eq));  // open: gt, lt
  and and_6 (and_6_out, A2_q[32], comparator_4_eq);
  assign Data_Out = and_6_out ? D2_q : 32'bz;  // Controlled_Buffer controlled_buffer_3
  Counter #(.max('hffffffff), .width(32)) counter_1 (
    .count(and_7_out), .clk(clock_11_out));  // open: load, D, Q, carry, up, clr
  and and_7 (and_7_out, In_Cache, not_1_out);
  and and_8 (and_8_out, ~In_Cache, not_1_out);  // AND_Gate
  Register #(.width(33)) A3 (.D({1'b1, addr_upd}), .en(decoder_1_out3), .Q(A3_q), .clk(clock_9_out), .clr(R));
  Clock clock_9 (.out(clock_9_out));
  Register #(.width(32)) D3 (.D(Data_In), .en(decoder_1_out3), .Q(D3_q), .clk(clock_10_out), .clr(R));
  Clock clock_10 (.out(clock_10_out));
  Clock clock_11 (.out(clock_11_out));
  Decoder #(.select(3)) decoder_1 (
    .out0(decoder_1_out0), .out1(decoder_1_out1), .out2(decoder_1_out2), .out3(decoder_1_out3),
    .out4(decoder_1_out4), .out5(decoder_1_out5), .out6(decoder_1_out6), .out7(decoder_1_out7),
    .sel(multiplexer_2_out), .en(replace_or_update));
  Comparator #(.width(32)) comparator_5 (.a(addr_rd), .b(A3_q[31:0]), .eq(comparator_5_eq));  // open: gt, lt
  and and_9 (and_9_out, A3_q[32], comparator_5_eq);
  assign Data_Out = and_9_out ? D3_q : 32'bz;  // Controlled_Buffer controlled_buffer_4
  Counter #(.max('hffffffff), .width(32)) counter_2 (
    .count(and_8_out), .clk(clock_11_out));  // open: load, D, Q, carry, up, clr
  Register #(.width(33)) A4 (.D({1'b1, addr_upd}), .en(decoder_1_out4), .Q(A4_q), .clk(clock_12_out), .clr(R));
  Clock clock_12 (.out(clock_12_out));
  Register #(.width(32)) D4 (.D(Data_In), .en(decoder_1_out4), .Q(D4_q), .clk(clock_13_out), .clr(R));
  Clock clock_13 (.out(clock_13_out));
  // Priority_Encoder priority_encoder_1: pin names not known; wires that end beside it: and_3_out, and_5_out, and_6_out, and_9_out, matching_Ax, priority_encoder_1_p6, In_Cache, priority_encoder_1_p8, priority_encoder_1_p9, priority_encoder_1_p10, 1'b1
  Comparator #(.width(32)) comparator_6 (.a(addr_rd), .b(A4_q[31:0]), .eq(comparator_6_eq));  // open: gt, lt
  and and_10 (priority_encoder_1_p6, A4_q[32], comparator_6_eq);
  assign Data_Out = priority_encoder_1_p6 ? D4_q : 32'bz;  // Controlled_Buffer controlled_buffer_5
  Register #(.width(33)) A5 (.D({1'b1, addr_upd}), .en(decoder_1_out5), .Q(A5_q), .clk(clock_14_out), .clr(R));
  Clock clock_14 (.out(clock_14_out));
  Register #(.width(32)) D5 (.D(Data_In), .en(decoder_1_out5), .Q(D5_q), .clk(clock_15_out), .clr(R));
  Clock clock_15 (.out(clock_15_out));
  Comparator #(.width(32)) comparator_7 (.a(addr_rd), .b(A5_q[31:0]), .eq(comparator_7_eq));  // open: gt, lt
  and and_11 (priority_encoder_1_p8, A5_q[32], comparator_7_eq);
  assign Data_Out = priority_encoder_1_p8 ? D5_q : 32'bz;  // Controlled_Buffer controlled_buffer_6
  Clock clock_16 (.out(clock_16_out));
  Clock clock_17 (.out(clock_17_out));
  Register #(.width(33)) A6 (.D({1'b1, addr_upd}), .en(decoder_1_out6), .Q(A6_q), .clk(clock_16_out), .clr(R));
  Register #(.width(32)) D6 (.D(Data_In), .en(decoder_1_out6), .Q(D6_q), .clk(clock_17_out), .clr(R));
  Comparator #(.width(32)) comparator_8 (.a(addr_rd), .b(A6_q[31:0]), .eq(comparator_8_eq));  // open: gt, lt
  and and_12 (priority_encoder_1_p9, A6_q[32], comparator_8_eq);
  assign Data_Out = priority_encoder_1_p9 ? D6_q : 32'bz;  // Controlled_Buffer controlled_buffer_7
  Clock clock_18 (.out(clock_18_out));
  Clock clock_19 (.out(clock_19_out));
  Register #(.width(33)) A7 (.D({1'b1, addr_upd}), .en(decoder_1_out7), .Q(A7_q), .clk(clock_18_out), .clr(R));
  and and_13 (priority_encoder_1_p10, A7_q[32], comparator_9_eq);
  Register #(.width(32)) D7 (.D(Data_In), .en(decoder_1_out7), .Q(D7_q), .clk(clock_19_out), .clr(R));
  Comparator #(.width(32)) comparator_9 (.a(addr_rd), .b(A7_q[31:0]), .eq(comparator_9_eq));  // open: gt, lt
  assign Data_Out = priority_encoder_1_p10 ? D7_q : 32'bz;  // Controlled_Buffer controlled_buffer_8

  // Other names for the same wires on the sheet: present_in_cache = In_Cache

  // Notes on the sheet:
  //   cache hits
  //   cache misses
endmodule
